# Fritzing sketch project one (saved by Fritzing 0.9.3b)
breadboards: 2

parts:
  LCD1 = LCD screen
  PSU1 = Adjustable Breadboard Power Supply
  R1 = Trimmer Potentiometer [maximum_resistance=10kΩ package=THT]
  Part1 = RFID-RC522-v2

nets:
  N1: LCD1.VSS, PSU1.Vin-, R1.leg2
  N2: LCD1.VDD, PSU1.Vin+, R1.leg1
  N3: LCD1.V0, R1.wiper
  N4: PSU1.Vout+, Part1.3.3V
  N5: PSU1.Vout-, Part1.RST

custom parts:
  RFID-RC522-v2: A simple China made RFID-RC522 Reader; do check the pin labels, as this is a MFRC522 based clone.
